# Fritzing sketch CABR (saved by Fritzing 0.9.3b)
breadboards: 1

parts:
  U2 = Voltage Regulator - 5V [part_number="This goes on backward to save space" package="TO220 [THT]"]
  C1 = Electrolytic Capacitor [capacitance=10µF voltage=20V package="100 mil [THT, electrolytic]"]
  C2 = Electrolytic Capacitor [capacitance=10µF voltage=20V package="100 mil [THT, electrolytic]"]
  Q2 = MOSFET-NCHANNEL [package=to220v]
  U1 = attiny85 [package=dip]
  J1 = Screw terminal - 2 pins [part_number=Power package=THT]
  R1 = Resistor [tolerance=±5% resistance=10k package="0805 [SMD]"]
  R3 = Vertical Resistor [tolerance=±5% resistance=10k package=THT]
  J3 = Screw terminal - 2 pins [part_number=Power package=THT]
  J4 = Screw terminal - 2 pins [package=THT]
  R4 = Vertical Resistor [tolerance=±5% resistance=10k package=THT]
  J2 = screw terminal, 3 pins
  D1 = Diode [package=diode-1n4001]
  R5 = Resistor [tolerance=±5% resistance=1k package="2512 [SMD]"]
  R6 = Vertical Resistor [tolerance=±5% resistance=10k package=THT]
  Q1 = NPN-Transistor [package="TO92 [THT]"]
  R7 = Vertical Resistor [tolerance=±5% resistance=1k package=THT]

nets:
  N1: U2.input_voltage, C2.+
  N2: U2.GND, C1.-, C2.-, Q2.G, U1.Pin_4, J1.pin2, R1.Pin_1, R3.Pin_0, R4.Pin_0, Q1.E, R7.Pin_0
  N3: U2.output_voltage, C1.+, J1.pin1, J3.pin1, D1.A, R6.Pin_0
  N4: Q2.D, R6.Pin_1
  N5: Q2.S, J3.pin2
  N6: U1.Pin_2, R5.Pin_0
  N7: U1.Pin_3, J4.pin2, R4.Pin_1
  N8: U1.Pin_6, R3.Pin_1, J2.pin1
  N9: U1.Pin_7, R1.Pin_0, J2.pin3
  N10: U1.Pin_8, J4.pin1, J2.pin2
  N11: R5.Pin_1, Q1.C, R7.Pin_1

notes:
  The Voltage regulator will go on backward to save space.

custom parts:
  Vertical Resistor: A generic resistor (0.25W)
